// Logisim project ALU.circ as structural Verilog: 3 circuits, main circuit ALU main
module ALU_main (
  input  [31:0] Rs,
  input  [31:0] Rt,
  input  [31:0] Shoosed,
  input  [3:0] Select_Op,
  input  [31:0] Hight,
  input  Hight_Op,
  input  Unsigned,
  output Great,
  output Equal,
  output Less
);

  wire C_Add, C_Rest, LessU, OpHight;
  wire [31:0] ADD, AND, DIV, Div_t, Divu, Mult, multiplexer_3_out, multiplexer_4_out, Mulu, NOR, OR, R_Div,
       R_Divu, R_Mult, R_Mulu, Slt, Sltu, SUB, XOR;

  assign AND = Rs & Rt;  // AND_Gate and_1, 32 bits wide
  assign OR = Rs | Rt;  // OR_Gate or_1, 32 bits wide
  assign XOR = Rs ^ Rt;  // XOR_Gate xor_1, 32 bits wide
  assign NOR = ~(Rs | Rt);  // NOR_Gate nor_1, 32 bits wide
  Adder #(.width(32)) adder_1 (.a(Rs), .b(Rt), .out(ADD), .cin(1'b0), .cout(C_Add));
  Subtractor #(.width(32)) subtractor_1 (.a(Rs), .b(Rt), .out(SUB), .bin(1'b0), .bout(C_Rest));
  Divu divu_1 (.in_1(Rs), .in_2(Rt), .out_3(Divu), .out_4(R_Divu));
  Comparator #(.width(32)) comparator_1 (.a(Rs), .b(Rt), .gt(Great), .eq(Equal), .lt(Less));
  Multiplexer #(.width(32), .enable("false")) multiplexer_1 (.in0({32{1'b0}}), .in1(32'h1), .out(Slt), .sel(Less));
  Multiplier #(.width(32)) multiplier_1 (.a(Rs), .b(Rt), .out(Mult), .cin({32{1'b0}}), .cout(R_Mult));
  Divider #(.width(32)) divider_1 (.a(Rs), .b(Rt), .out(DIV), .upper({32{1'b0}}), .rem(R_Div));
  Mulu mulu_1 (.in_1(Rs), .in_2(Rt), .out_3(Mulu), .out_4(R_Mulu));
  Comparator #(.width(32), .mode("unsigned")) comparator_2 (.a(Rs), .b(Rt), .lt(LessU));  // open: gt, eq
  Multiplexer #(.width(32), .enable("false")) multiplexer_2 (.in0({32{1'b0}}), .in1(32'h1), .out(Sltu), .sel(LessU));
  Multiplexer #(.width(32), .enable("false")) multiplexer_3 (
    .in0(R_Mult), .in1(R_Mulu), .out(multiplexer_3_out), .sel(Unsigned));
  Multiplexer #(.width(32), .enable("false")) multiplexer_4 (
    .in0(R_Div), .in1(R_Divu), .out(multiplexer_4_out), .sel(Unsigned));
  Multiplexer #(.select(4), .width(32), .enable("false")) multiplexer_5 (
    .in0(ADD), .in1(SUB), .in2(Mult), .in3(Mulu), .in4(Divu), .in5(Div_t), .in6(AND), .in7(OR), .in8(NOR),
    .in9(XOR), .in10(Slt), .in11(Sltu), .out(Shoosed), .sel(Select_Op));  // open: in12, in13, in14, in15
  Multiplexer #(.width(32), .enable("false")) multiplexer_6 (
    .in0(multiplexer_3_out), .in1(multiplexer_4_out), .out(Hight), .sel(OpHight));

  // Other names for the same wires on the sheet: A[31:0] = Rs; B[31:0] = Rt; Hi_S[31:0] = Hight; OpHight_t = Hight_Op

  // Notes on the sheet:
  //   Entradas
  //   Logical Operations
  //   Aritmetic Operations
  //   Comparers
  //   General Shooser
  //   Hight Shooser
  //   Exits
endmodule

module Mulu (
  input  [31:0] in_1,
  input  [31:0] in_2,
  output [31:0] out_3,
  output [31:0] out_4
);

  assign out_3 = in_1 & in_2;  // AND_Gate and_1, 32 bits wide

  assign out_4 = out_3;
endmodule

module Divu (
  input  [31:0] in_1,
  input  [31:0] in_2,
  output [31:0] out_3,
  output [31:0] out_4
);

  assign out_3 = in_1 | in_2;  // OR_Gate or_1, 32 bits wide

  assign out_4 = out_3;
endmodule
